// Logisim project Proyecto.circ as structural Verilog
module MIR (
  input  [35:0] MICROINSTRUCCION,
  input  CLK,
  output [3:0] B,
  output [2:0] MEM,
  output [8:0] C,
  output [7:0] ALU,
  output JAMZ,
  output JAMN,
  output JMPC,
  output [8:0] ADDR,
  output [2:0] JAM
);

  Register #(.trigger("falling"), .width(36)) register_1 (
    .D(MICROINSTRUCCION), .en(1'b1), .clk(CLK), .Q({ADDR, JMPC, JAMN, JAMZ, ALU, C, MEM, B}), .clr(1'b0));
endmodule

module DECODIFICADOR_B (
  input  [3:0] B,
  output MDR,
  output PC,
  output MBR,
  output MBRU,
  output SP,
  output LV,
  output CPP,
  output TOS,
  output OPC
);

  Decoder #(.enable("false"), .select(4)) decoder_1 (
    .out0(MDR), .out1(PC), .out2(MBR), .out3(MBRU), .out4(SP), .out5(LV), .out6(CPP), .out7(TOS), .out8(OPC),
    .sel(B));  // open: out9, out10, out11, out12, out13, out14, out15
endmodule

module LOGICA_MPC (
  input  [7:0] MBR,
  input  JMPC,
  input  [8:0] ADDR,
  input  JAMZ,
  input  Z,
  input  JAMN,
  input  N,
  output [8:0] PROXIMA_DIRECCION
);

  wire and_1_out, and_2_out;
  wire [7:0] multiplexer_1_out;

  Multiplexer #(.width(8)) multiplexer_1 (.in0({8{1'b0}}), .in1(MBR), .out(multiplexer_1_out), .sel(JMPC));
  assign PROXIMA_DIRECCION[7:0] = multiplexer_1_out | ADDR[7:0];  // OR_Gate or_1, 8 bits wide
  and and_1 (and_1_out, JAMZ, Z);
  and and_2 (and_2_out, JAMN, N);
  or or_2 (PROXIMA_DIRECCION[8], ADDR[8], and_1_out, and_2_out);
endmodule

module MPC (
  input  [8:0] PROXIMA_DIRECCION,
  input  CLK,
  output [8:0] DIRECCION_ROM
);

  Register #(.trigger("high"), .width(9)) register_1 (
    .D(PROXIMA_DIRECCION), .en(1'b1), .clk(CLK), .Q(DIRECCION_ROM), .clr(1'b0));
endmodule

module MEMORIA_CONTROL (
  input  [8:0] DIRECCION_ROM,
  output [35:0] MICROINSTRUCCION
);

  ROM #(.addrWidth(9), .dataWidth(36)) rom_1 (.addr(DIRECCION_ROM), .data(MICROINSTRUCCION));

  // Notes on the sheet:
  //   contents of rom_1 (hex, n*v repeats v):
  //   aadccaaea 123456789
endmodule

module UNIDAD_CONTROL (
  input  CLK,
  input  [7:0] MBR_DATO,
  input  Z,
  input  N,
  output [7:0] ALU_CONTROL,
  output [8:0] C_CONTROL,
  output [2:0] MEM_CONTROL,
  output [35:0] MICROINSTRUCCION_ACTUAL,
  output [8:0] DIRECCION_ACTUAL,
  output B_MDR,
  output B_PC,
  output B_MBR,
  output B_MBRU,
  output B_SP,
  output B_LV,
  output B_CPP,
  output B_TOS,
  output B_OPC,
  output [8:0] PROXIMA_CALCULADA
);

  wire mir_1_jamn, mir_1_jamz, mir_1_jmpc;
  wire [3:0] mir_1_b;
  wire [8:0] mir_1_addr;

  MPC mpc_1 (.PROXIMA_DIRECCION(PROXIMA_CALCULADA), .CLK(CLK), .DIRECCION_ROM(DIRECCION_ACTUAL));
  MEMORIA_CONTROL memoria_control_1 (.DIRECCION_ROM(DIRECCION_ACTUAL), .MICROINSTRUCCION(MICROINSTRUCCION_ACTUAL));
  MIR mir_1 (
    .MICROINSTRUCCION(MICROINSTRUCCION_ACTUAL), .CLK(CLK), .B(mir_1_b), .MEM(MEM_CONTROL), .C(C_CONTROL),
    .ALU(ALU_CONTROL), .JAMZ(mir_1_jamz), .JAMN(mir_1_jamn), .JMPC(mir_1_jmpc), .ADDR(mir_1_addr));  // open: JAM
  LOGICA_MPC logica_mpc_1 (
    .MBR(MBR_DATO), .JMPC(mir_1_jmpc), .ADDR(mir_1_addr), .JAMZ(mir_1_jamz), .Z(Z), .JAMN(mir_1_jamn), .N(N),
    .PROXIMA_DIRECCION(PROXIMA_CALCULADA));
  DECODIFICADOR_B decodificador_b_1 (
    .B(mir_1_b), .MDR(B_MDR), .PC(B_PC), .MBR(B_MBR), .MBRU(B_MBRU), .SP(B_SP), .LV(B_LV), .CPP(B_CPP),
    .TOS(B_TOS), .OPC(B_OPC));
endmodule
