// Logisim project base_profe.circ as structural Verilog: 23 circuits, main circuit main
module main (
  input  CLK,
  output [31:0] PC,
  output [8:0] MPC,
  output [31:0] B,
  output [31:0] C
);

  wire control_unit_4d35bd06_1_cpp_b, control_unit_4d35bd06_1_cpp_c, control_unit_4d35bd06_1_h_c,
       control_unit_4d35bd06_1_lv_b, control_unit_4d35bd06_1_lv_c, control_unit_4d35bd06_1_mar_c,
       control_unit_4d35bd06_1_mbr_b, control_unit_4d35bd06_1_mbru_b, control_unit_4d35bd06_1_mdr_b,
       control_unit_4d35bd06_1_mdr_c, control_unit_4d35bd06_1_opc_b, control_unit_4d35bd06_1_opc_c,
       control_unit_4d35bd06_1_pc_b, control_unit_4d35bd06_1_pc_c, control_unit_4d35bd06_1_sp_b,
       control_unit_4d35bd06_1_sp_c, control_unit_4d35bd06_1_tos_b, control_unit_4d35bd06_1_tos_c,
       data_path_f5cf4019_1_n, data_path_f5cf4019_1_z, RESET_out;
  wire [1:0] control_unit_4d35bd06_1_alu_2, control_unit_4d35bd06_1_shifter;
  wire [2:0] control_unit_4d35bd06_1_mem;
  wire [3:0] control_unit_4d35bd06_1_alu;
  wire [7:0] data_path_f5cf4019_1_op_code, mem_1_mem_fetch;
  wire [31:0] data_path_f5cf4019_1_mem_mar, data_path_f5cf4019_1_mem_wr, mem_1_mrm_rd;

  Mem mem_1 (
    .CLK(CLK), .MEM_ADDR_32(data_path_f5cf4019_1_mem_mar), .MEM_ADDR_8(PC),
    .wr(control_unit_4d35bd06_1_mem[2]), .rd(control_unit_4d35bd06_1_mem[1]),
    .fetch(control_unit_4d35bd06_1_mem[0]), .MEM_WR(data_path_f5cf4019_1_mem_wr), .MRM_RD(mem_1_mrm_rd),
    .MEM_FETCH(mem_1_mem_fetch));
  Button RESET (.out(RESET_out));
  Data_Path_f5cf4019 data_path_f5cf4019_1 (
    .MEM_RD(mem_1_mrm_rd), .rd(control_unit_4d35bd06_1_mem[1]), .MEM_FETCH(mem_1_mem_fetch),
    .RESET(RESET_out), .CLK(CLK), .MDR_C(control_unit_4d35bd06_1_mdr_c), .PC_C(control_unit_4d35bd06_1_pc_c),
    .fetch(control_unit_4d35bd06_1_mem[0]), .SP_C(control_unit_4d35bd06_1_sp_c),
    .LV_C(control_unit_4d35bd06_1_lv_c), .CPP_C(control_unit_4d35bd06_1_cpp_c),
    .TOS_C(control_unit_4d35bd06_1_tos_c), .OPC_C(control_unit_4d35bd06_1_opc_c),
    .MAR_C(control_unit_4d35bd06_1_mar_c), .H_C(control_unit_4d35bd06_1_h_c),
    .SRA1(control_unit_4d35bd06_1_shifter[0]), .SLL8(control_unit_4d35bd06_1_shifter[1]),
    .ENA(control_unit_4d35bd06_1_alu[3]), .ENB(control_unit_4d35bd06_1_alu[2]),
    .F(control_unit_4d35bd06_1_alu_2), .CIN(control_unit_4d35bd06_1_alu[0]),
    .INVA(control_unit_4d35bd06_1_alu[1]), .MBR(control_unit_4d35bd06_1_mbr_b),
    .MBRU(control_unit_4d35bd06_1_mbru_b), .MDR_B(control_unit_4d35bd06_1_mdr_b),
    .PC_B(control_unit_4d35bd06_1_pc_b), .SP_B(control_unit_4d35bd06_1_sp_b),
    .LV_B(control_unit_4d35bd06_1_lv_b), .CPP_B(control_unit_4d35bd06_1_cpp_b),
    .TOS_B(control_unit_4d35bd06_1_tos_b), .OPC_B(control_unit_4d35bd06_1_opc_b), .MEM_PC(PC),
    .N(data_path_f5cf4019_1_n), .Z(data_path_f5cf4019_1_z), .B(B), .C(C),
    .MEM_WR(data_path_f5cf4019_1_mem_wr), .OP_CODE(data_path_f5cf4019_1_op_code),
    .MEM_MAR(data_path_f5cf4019_1_mem_mar));
  Control_Unit_4d35bd06 control_unit_4d35bd06_1 (
    .Z(data_path_f5cf4019_1_z), .N(data_path_f5cf4019_1_n), .CLK(CLK), .MBR(data_path_f5cf4019_1_op_code),
    .RESET(RESET_out), .MAR_C(control_unit_4d35bd06_1_mar_c), .H_C(control_unit_4d35bd06_1_h_c),
    .OPC_C(control_unit_4d35bd06_1_opc_c), .TOS_C(control_unit_4d35bd06_1_tos_c),
    .CPP_C(control_unit_4d35bd06_1_cpp_c), .LV_C(control_unit_4d35bd06_1_lv_c),
    .SP_C(control_unit_4d35bd06_1_sp_c), .PC_C(control_unit_4d35bd06_1_pc_c), .out_6(MPC),
    .MDR_B(control_unit_4d35bd06_1_mdr_b), .PC_B(control_unit_4d35bd06_1_pc_b),
    .MBR_B(control_unit_4d35bd06_1_mbr_b), .MBRU_B(control_unit_4d35bd06_1_mbru_b),
    .SP_B(control_unit_4d35bd06_1_sp_b), .LV_B(control_unit_4d35bd06_1_lv_b),
    .CPP_B(control_unit_4d35bd06_1_cpp_b), .TOS_B(control_unit_4d35bd06_1_tos_b),
    .OPC_B(control_unit_4d35bd06_1_opc_b), .Mem(control_unit_4d35bd06_1_mem),
    .ALU({control_unit_4d35bd06_1_alu_2, control_unit_4d35bd06_1_alu}),
    .Shifter(control_unit_4d35bd06_1_shifter), .MDR_C(control_unit_4d35bd06_1_mdr_c));
endmodule

module Mem (
  input  wr,
  input  [31:0] MEM_WR,
  input  [31:0] MEM_ADDR_32,
  input  rd,
  input  [31:0] MEM_ADDR_8,
  input  fetch,
  input  CLK,
  output [31:0] MRM_RD,
  output [7:0] MEM_FETCH
);

  wire not_1_out, not_2_out, not_3_out;
  wire [7:0] ram_2_data;
  wire [31:0] ram_1_data;

  not not_1 (not_1_out, CLK);
  not not_2 (not_2_out, wr);
  RAM #(.addrWidth(24), .dataWidth(32)) ram_1 (
    .addr(MEM_ADDR_32[23:0]), .data(ram_1_data), .sel(1'b1), .clk(not_1_out), .ld(not_2_out), .clr(1'b0));
  assign ram_1_data = wr ? MEM_WR : 32'bz;  // Controlled_Buffer controlled_buffer_1
  assign MRM_RD = rd ? ram_1_data : 32'bz;  // Controlled_Buffer controlled_buffer_2
  not not_3 (not_3_out, CLK);
  assign MEM_FETCH = fetch ? ram_2_data : 8'bz;  // Controlled_Buffer controlled_buffer_3
  RAM #(.addrWidth(24)) ram_2 (
    .addr(MEM_ADDR_8[23:0]), .data(ram_2_data), .sel(1'b1), .clk(not_3_out), .clr(1'b0));  // open: ld

  // Notes on the sheet:
  //   Una truchada porque Logisim no tiene
  //   un bloque de memoria con dos canales de datos
endmodule

module Control_Unit_4d35bd06 (
  input  CLK,
  input  RESET,
  input  [7:0] MBR,
  input  N,
  input  Z,
  output [8:0] out_6,
  output MDR_B,
  output PC_B,
  output MBR_B,
  output MBRU_B,
  output SP_B,
  output LV_B,
  output CPP_B,
  output TOS_B,
  output OPC_B,
  output [2:0] Mem,
  output [5:0] ALU,
  output [1:0] Shifter,
  output H_C,
  output OPC_C,
  output TOS_C,
  output CPP_C,
  output LV_C,
  output SP_C,
  output PC_C,
  output MDR_C,
  output MAR_C
);

  wire and_1_out, and_2_out, d_flipflop_asc_3e1d20b5_1_q, d_flipflop_asc_3e1d20b5_2_q, not_1_out;
  wire [2:0] mir_1_jam;
  wire [3:0] control_store_319429ec_1_cs_s4, mir_1_b;
  wire [7:0] mir_1_addr, multiplexer_3_out, or_2_out;
  wire [8:0] multiplexer_1_out, multiplexer_2_out;
  wire [8:8] mir_1_addr_2, or_1_out;
  wire [31:0] control_store_319429ec_1_cs_s32;

  Multiplexer #(.width(9)) multiplexer_1 (.in0({9{1'b1}}), .in1(9'hff), .out(multiplexer_1_out), .sel(RESET));
  Multiplexer #(.width(9)) multiplexer_2 (.in0({9{1'b1}}), .in1(9'h100), .out(multiplexer_2_out), .sel(RESET));
  and and_1 (and_1_out, d_flipflop_asc_3e1d20b5_1_q, mir_1_jam[1]);
  D_FlipFlop_Asc_3e1d20b5 d_flipflop_asc_3e1d20b5_1 (
    .D(N), .CLK(CLK), .L_CLR_53bffd8b(not_1_out), .L_PRE_100dd675(1'b1), .Q(d_flipflop_asc_3e1d20b5_1_q));  // open: L_Q_e415d1a6
  D_FlipFlop_Asc_3e1d20b5 d_flipflop_asc_3e1d20b5_2 (
    .D(Z), .CLK(CLK), .L_CLR_53bffd8b(not_1_out), .L_PRE_100dd675(1'b1), .Q(d_flipflop_asc_3e1d20b5_2_q));  // open: L_Q_e415d1a6
  Multiplexer #(.width(8)) multiplexer_3 (
    .in0(mir_1_addr), .in1(or_2_out), .out(multiplexer_3_out), .sel(mir_1_jam[2]));
  or or_1 (or_1_out[8], and_1_out, and_2_out, mir_1_addr_2[8]);
  and and_2 (and_2_out, d_flipflop_asc_3e1d20b5_2_q, mir_1_jam[0]);
  assign or_2_out = MBR | mir_1_addr;  // OR_Gate or_2, 8 bits wide
  not not_1 (not_1_out, RESET);
  MPC mpc_1 (
    .CLK(CLK), .Entrada({or_1_out[8], multiplexer_3_out}), .L_PRE_100dd675(multiplexer_1_out),
    .L_CLR_53bffd8b(multiplexer_2_out), .Salida(out_6));
  Control_Store_319429ec control_store_319429ec_1 (
    .CS_E(out_6), .CS_S32(control_store_319429ec_1_cs_s32), .CS_S4(control_store_319429ec_1_cs_s4));
  MIR mir_1 (
    .Entrada_4(control_store_319429ec_1_cs_s4), .Entrada_32(control_store_319429ec_1_cs_s32), .CLK(CLK),
    .RESET(RESET), .B(mir_1_b), .Mem(Mem), .C({H_C, OPC_C, TOS_C, CPP_C, LV_C, SP_C, PC_C, MDR_C, MAR_C}),
    .ALU({Shifter, ALU}), .JAM(mir_1_jam), .Addr({mir_1_addr_2[8], mir_1_addr}));
  Decoder #(.enable("false"), .select(4)) decoder_1 (
    .out0(MDR_B), .out1(PC_B), .out2(MBR_B), .out3(MBRU_B), .out4(SP_B), .out5(LV_B), .out6(CPP_B),
    .out7(TOS_B), .out8(OPC_B), .sel(mir_1_b));  // open: out9, out10, out11, out12, out13, out14, out15
endmodule

module Control_Store_319429ec (
  input  [8:0] CS_E,
  output [31:0] CS_S32,
  output [3:0] CS_S4
);

  ROM #(.addrWidth(9), .dataWidth(32)) rom_1 (.addr(CS_E), .data(CS_S32), .sel(1'b1));
  ROM #(.addrWidth(9), .dataWidth(4)) rom_2 (.addr(CS_E), .data(CS_S4), .sel(1'b1));

  // Notes on the sheet:
  //   Otra truchada porque Logisim no tiene
  //   un bloque de memoria mas ancho que 32 bits
  //   contents of rom_1 (hex, n*v repeats v):
  //   80000000 255*0 435021
  //   contents of rom_2 (hex, n*v repeats v):
  //   f 255*0 1
endmodule

module MPC (
  input  [8:0] L_PRE_100dd675,
  input  [8:0] Entrada,
  input  CLK,
  input  [8:0] L_CLR_53bffd8b,
  output [8:0] Salida
);

  D_Latch_70c0f4da d_latch_70c0f4da_1 (
    .D(Entrada[8]), .EN(CLK), .L_PRE_100dd675(L_PRE_100dd675[8]), .L_CLR_53bffd8b(L_CLR_53bffd8b[8]),
    .Q(Salida[8]));  // open: L_Q_e415d1a6
  D_Latch_70c0f4da d_latch_70c0f4da_2 (
    .D(Entrada[7]), .EN(CLK), .L_PRE_100dd675(L_PRE_100dd675[7]), .L_CLR_53bffd8b(L_CLR_53bffd8b[7]),
    .Q(Salida[7]));  // open: L_Q_e415d1a6
  D_Latch_70c0f4da d_latch_70c0f4da_3 (
    .D(Entrada[6]), .EN(CLK), .L_PRE_100dd675(L_PRE_100dd675[6]), .L_CLR_53bffd8b(L_CLR_53bffd8b[6]),
    .Q(Salida[6]));  // open: L_Q_e415d1a6
  D_Latch_70c0f4da d_latch_70c0f4da_4 (
    .D(Entrada[5]), .EN(CLK), .L_PRE_100dd675(L_PRE_100dd675[5]), .L_CLR_53bffd8b(L_CLR_53bffd8b[5]),
    .Q(Salida[5]));  // open: L_Q_e415d1a6
  D_Latch_70c0f4da d_latch_70c0f4da_5 (
    .D(Entrada[4]), .EN(CLK), .L_PRE_100dd675(L_PRE_100dd675[4]), .L_CLR_53bffd8b(L_CLR_53bffd8b[4]),
    .Q(Salida[4]));  // open: L_Q_e415d1a6
  D_Latch_70c0f4da d_latch_70c0f4da_6 (
    .D(Entrada[3]), .EN(CLK), .L_PRE_100dd675(L_PRE_100dd675[3]), .L_CLR_53bffd8b(L_CLR_53bffd8b[3]),
    .Q(Salida[3]));  // open: L_Q_e415d1a6
  D_Latch_70c0f4da d_latch_70c0f4da_7 (
    .D(Entrada[2]), .EN(CLK), .L_PRE_100dd675(L_PRE_100dd675[2]), .L_CLR_53bffd8b(L_CLR_53bffd8b[2]),
    .Q(Salida[2]));  // open: L_Q_e415d1a6
  D_Latch_70c0f4da d_latch_70c0f4da_8 (
    .D(Entrada[1]), .EN(CLK), .L_PRE_100dd675(L_PRE_100dd675[1]), .L_CLR_53bffd8b(L_CLR_53bffd8b[1]),
    .Q(Salida[1]));  // open: L_Q_e415d1a6
  D_Latch_70c0f4da d_latch_70c0f4da_9 (
    .D(Entrada[0]), .EN(CLK), .L_PRE_100dd675(L_PRE_100dd675[0]), .L_CLR_53bffd8b(L_CLR_53bffd8b[0]),
    .Q(Salida[0]));  // open: L_Q_e415d1a6
endmodule

module MIR (
  input  [3:0] Entrada_4,
  input  [31:0] Entrada_32,
  input  CLK,
  input  RESET,
  output [3:0] B,
  output [2:0] Mem,
  output [8:0] C,
  output [7:0] ALU,
  output [2:0] JAM,
  output [8:0] Addr
);

  wire [3:0] multiplexer_2_out, multiplexer_4_out, not_2_out;
  wire [31:0] multiplexer_1_out, multiplexer_3_out, not_1_out;

  Multiplexer #(.width(32)) multiplexer_1 (.in0({32{1'b1}}), .in1(not_1_out), .out(multiplexer_1_out), .sel(RESET));
  assign not_1_out = ~32'h435021;  // NOT_Gate not_1, 32 bits wide
  assign not_2_out = ~4'b0001;  // NOT_Gate not_2, 4 bits wide
  Multiplexer #(.width(4)) multiplexer_2 (.in0(4'b1111), .in1(not_2_out), .out(multiplexer_2_out), .sel(RESET));
  Multiplexer #(.width(32)) multiplexer_3 (.in0({32{1'b1}}), .in1(32'h435021), .out(multiplexer_3_out), .sel(RESET));
  Multiplexer #(.width(4)) multiplexer_4 (.in0(4'b1111), .in1(4'b0001), .out(multiplexer_4_out), .sel(RESET));
  Register_32_bits_Des_7310dea0 register_32_bits_des_7310dea0_1 (
    .CLK(CLK), .Entrada(Entrada_32), .L_PRE_100dd675(multiplexer_1_out), .L_CLR_53bffd8b(multiplexer_3_out),
    .Salida({Addr, JAM, ALU, C, Mem}));
  Register_4_bits_Des_d9ff5b2d register_4_bits_des_d9ff5b2d_1 (
    .CLK(CLK), .Entrada(Entrada_4), .L_PRE_100dd675(multiplexer_2_out), .L_CLR_53bffd8b(multiplexer_4_out),
    .Salida(B));
endmodule

module Data_Path_f5cf4019 (
  input  MAR_C,
  input  [31:0] MEM_RD,
  input  MDR_B,
  input  MDR_C,
  input  rd,
  input  PC_B,
  input  [7:0] MEM_FETCH,
  input  PC_C,
  input  MBR,
  input  fetch,
  input  MBRU,
  input  SP_C,
  input  SP_B,
  input  LV_B,
  input  LV_C,
  input  CPP_B,
  input  CPP_C,
  input  RESET,
  input  TOS_B,
  input  TOS_C,
  input  OPC_B,
  input  OPC_C,
  input  H_C,
  input  CLK,
  input  CIN,
  input  INVA,
  input  ENA,
  input  ENB,
  input  [1:0] F,
  input  SRA1,
  input  SLL8,
  output [31:0] MEM_MAR,
  output [31:0] MEM_WR,
  output [31:0] MEM_PC,
  output [7:0] OP_CODE,
  output [31:0] B,
  output N,
  output Z,
  output [31:0] C
);

  wire [7:0] multiplexer_1_out, undriven;
  wire [31:0] alu_32bits_1_s, multiplexer_2_out, multiplexer_3_out,
       register_32_bits_hold_paralel_load_899275db_1_salida,
       register_32_bits_hold_paralel_load_899275db_4_salida,
       register_32_bits_hold_paralel_load_899275db_5_salida,
       register_32_bits_hold_paralel_load_899275db_6_salida,
       register_32_bits_hold_paralel_load_899275db_7_salida,
       register_32_bits_hold_paralel_load_899275db_8_salida,
       register_32_bits_hold_paralel_load_899275db_9_salida;

  Multiplexer #(.width(8)) multiplexer_1 (.in0({8{1'b1}}), .in1({8{1'b0}}), .out(multiplexer_1_out), .sel(RESET));
  Multiplexer #(.width(32)) multiplexer_2 (.in0({32{1'b1}}), .in1({32{1'b0}}), .out(multiplexer_2_out), .sel(RESET));
  Multiplexer #(.width(32)) multiplexer_3 (.in0(C), .in1(MEM_RD), .out(multiplexer_3_out), .sel(rd));
  Register_8_bits_Hold_Paralel_Load_15446fa9 register_8_bits_hold_paralel_load_15446fa9_1 (
    .LOAD(CLK), .CLK(fetch), .Entrada(MEM_FETCH), .L_PRE_100dd675(undriven),
    .L_CLR_53bffd8b(multiplexer_1_out), .Salida(OP_CODE));
  Register_32_bits_Hold_Paralel_Load_899275db register_32_bits_hold_paralel_load_899275db_1 (
    .Entrada(C), .LOAD(MAR_C), .CLK(CLK), .L_PRE_ecaf25db({32{1'b1}}), .L_CLR_943e0add(multiplexer_2_out),
    .Salida(register_32_bits_hold_paralel_load_899275db_1_salida));
  assign B = MDR_B ? MEM_WR : 32'bz;  // Controlled_Buffer controlled_buffer_1
  Register_32_bits_Hold_Paralel_Load_899275db register_32_bits_hold_paralel_load_899275db_2 (
    .Entrada(multiplexer_3_out), .LOAD(MDR_C), .CLK(CLK), .L_PRE_ecaf25db({32{1'b1}}),
    .L_CLR_943e0add(multiplexer_2_out), .Salida(MEM_WR));
  assign B = PC_B ? MEM_PC : 32'bz;  // Controlled_Buffer controlled_buffer_2
  Register_32_bits_Hold_Paralel_Load_899275db register_32_bits_hold_paralel_load_899275db_3 (
    .Entrada(C), .LOAD(PC_C), .CLK(CLK), .L_PRE_ecaf25db({32{1'b1}}), .L_CLR_943e0add(multiplexer_2_out),
    .Salida(MEM_PC));
  MBR_EN_28495f5d mbr_en_28495f5d_1 (
    .in_1(OP_CODE), .MRB(MBR), .MBRU(MBRU), .Salida_Signada_7cd268af(B), .Salida_No_Signada_cc90b148(B));
  assign B = SP_B ? register_32_bits_hold_paralel_load_899275db_4_salida : 32'bz;  // Controlled_Buffer controlled_buffer_3
  Register_32_bits_Hold_Paralel_Load_899275db register_32_bits_hold_paralel_load_899275db_4 (
    .Entrada(C), .LOAD(SP_C), .CLK(CLK), .L_PRE_ecaf25db({32{1'b1}}), .L_CLR_943e0add(multiplexer_2_out),
    .Salida(register_32_bits_hold_paralel_load_899275db_4_salida));
  assign B = LV_B ? register_32_bits_hold_paralel_load_899275db_5_salida : 32'bz;  // Controlled_Buffer controlled_buffer_4
  Register_32_bits_Hold_Paralel_Load_899275db register_32_bits_hold_paralel_load_899275db_5 (
    .Entrada(C), .LOAD(LV_C), .CLK(CLK), .L_PRE_ecaf25db({32{1'b1}}), .L_CLR_943e0add(multiplexer_2_out),
    .Salida(register_32_bits_hold_paralel_load_899275db_5_salida));
  assign B = CPP_B ? register_32_bits_hold_paralel_load_899275db_6_salida : 32'bz;  // Controlled_Buffer controlled_buffer_5
  Register_32_bits_Hold_Paralel_Load_899275db register_32_bits_hold_paralel_load_899275db_6 (
    .Entrada(C), .LOAD(CPP_C), .CLK(CLK), .L_PRE_ecaf25db({32{1'b1}}), .L_CLR_943e0add(multiplexer_2_out),
    .Salida(register_32_bits_hold_paralel_load_899275db_6_salida));
  assign B = TOS_B ? register_32_bits_hold_paralel_load_899275db_7_salida : 32'bz;  // Controlled_Buffer controlled_buffer_6
  Register_32_bits_Hold_Paralel_Load_899275db register_32_bits_hold_paralel_load_899275db_7 (
    .Entrada(C), .LOAD(TOS_C), .CLK(CLK), .L_PRE_ecaf25db({32{1'b1}}), .L_CLR_943e0add(multiplexer_2_out),
    .Salida(register_32_bits_hold_paralel_load_899275db_7_salida));
  assign B = OPC_B ? register_32_bits_hold_paralel_load_899275db_8_salida : 32'bz;  // Controlled_Buffer controlled_buffer_7
  Register_32_bits_Hold_Paralel_Load_899275db register_32_bits_hold_paralel_load_899275db_8 (
    .Entrada(C), .LOAD(OPC_C), .CLK(CLK), .L_PRE_ecaf25db({32{1'b1}}), .L_CLR_943e0add(multiplexer_2_out),
    .Salida(register_32_bits_hold_paralel_load_899275db_8_salida));
  Register_32_bits_Hold_Paralel_Load_899275db register_32_bits_hold_paralel_load_899275db_9 (
    .Entrada(C), .LOAD(H_C), .CLK(CLK), .L_PRE_ecaf25db({32{1'b1}}), .L_CLR_943e0add(multiplexer_2_out),
    .Salida(register_32_bits_hold_paralel_load_899275db_9_salida));
  desplazador_MAR desplazador_mar_1 (.ENTRADA(register_32_bits_hold_paralel_load_899275db_1_salida), .SALIDA(MEM_MAR));
  Desplazador desplazador_1 (.SRA1(SRA1), .SLL8(SLL8), .Entrada(alu_32bits_1_s), .Salida(C));
  ALU_32bits alu_32bits_1 (
    .B(B), .A(register_32_bits_hold_paralel_load_899275db_9_salida), .Cin(CIN), .INVA(INVA), .ENA(ENA),
    .ENB(ENB), .F0_F1_db35ba42(F), .COUT(N), .S(alu_32bits_1_s));
  not not_1 (Z, N);

  // Notes on the sheet:
  //   Preset 8 Bits
  //   Clear 8 Bits
  //   Preset 32 Bits
  //   Clear 32 Bits
  //   Bus B
  //   Bus C
endmodule

module Register_32_bits_Hold_Paralel_Load_899275db (
  input  [31:0] L_PRE_ecaf25db,
  input  [31:0] Entrada,
  input  LOAD,
  input  CLK,
  input  [31:0] L_CLR_943e0add,
  output [31:0] Salida
);

  Register_8_bits_Hold_Paralel_Load_15446fa9 register_8_bits_hold_paralel_load_15446fa9_1 (
    .LOAD(CLK), .CLK(LOAD), .Entrada(Entrada[7:0]), .L_PRE_100dd675(L_PRE_ecaf25db[7:0]),
    .L_CLR_53bffd8b(L_CLR_943e0add[7:0]), .Salida(Salida[7:0]));
  Register_8_bits_Hold_Paralel_Load_15446fa9 register_8_bits_hold_paralel_load_15446fa9_2 (
    .LOAD(CLK), .CLK(LOAD), .Entrada(Entrada[15:8]), .L_PRE_100dd675(L_PRE_ecaf25db[15:8]),
    .L_CLR_53bffd8b(L_CLR_943e0add[15:8]), .Salida(Salida[15:8]));
  Register_8_bits_Hold_Paralel_Load_15446fa9 register_8_bits_hold_paralel_load_15446fa9_3 (
    .LOAD(CLK), .CLK(LOAD), .Entrada(Entrada[23:16]), .L_PRE_100dd675(L_PRE_ecaf25db[23:16]),
    .L_CLR_53bffd8b(L_CLR_943e0add[23:16]), .Salida(Salida[23:16]));
  Register_8_bits_Hold_Paralel_Load_15446fa9 register_8_bits_hold_paralel_load_15446fa9_4 (
    .LOAD(CLK), .CLK(LOAD), .Entrada(Entrada[31:24]), .L_PRE_100dd675(L_PRE_ecaf25db[31:24]),
    .L_CLR_53bffd8b(L_CLR_943e0add[31:24]), .Salida(Salida[31:24]));
endmodule

module Register_32_bits_Des_7310dea0 (
  input  [31:0] L_PRE_100dd675,
  input  [31:0] Entrada,
  input  CLK,
  input  [31:0] L_CLR_53bffd8b,
  output [31:0] Salida
);

  D_FlipFlop_Des_04483694 d_flipflop_des_04483694_1 (
    .D(Entrada[31]), .CLK(CLK), .L_PRE_100dd675(L_PRE_100dd675[31]), .L_CLR_53bffd8b(L_CLR_53bffd8b[31]),
    .Q(Salida[31]));  // open: L_Q_e415d1a6
  D_FlipFlop_Des_04483694 d_flipflop_des_04483694_2 (
    .D(Entrada[30]), .CLK(CLK), .L_PRE_100dd675(L_PRE_100dd675[30]), .L_CLR_53bffd8b(L_CLR_53bffd8b[30]),
    .Q(Salida[30]));  // open: L_Q_e415d1a6
  D_FlipFlop_Des_04483694 d_flipflop_des_04483694_3 (
    .D(Entrada[29]), .CLK(CLK), .L_PRE_100dd675(L_PRE_100dd675[29]), .L_CLR_53bffd8b(L_CLR_53bffd8b[29]),
    .Q(Salida[29]));  // open: L_Q_e415d1a6
  D_FlipFlop_Des_04483694 d_flipflop_des_04483694_4 (
    .D(Entrada[28]), .CLK(CLK), .L_PRE_100dd675(L_PRE_100dd675[28]), .L_CLR_53bffd8b(L_CLR_53bffd8b[28]),
    .Q(Salida[28]));  // open: L_Q_e415d1a6
  D_FlipFlop_Des_04483694 d_flipflop_des_04483694_5 (
    .D(Entrada[27]), .CLK(CLK), .L_PRE_100dd675(L_PRE_100dd675[27]), .L_CLR_53bffd8b(L_CLR_53bffd8b[27]),
    .Q(Salida[27]));  // open: L_Q_e415d1a6
  D_FlipFlop_Des_04483694 d_flipflop_des_04483694_6 (
    .D(Entrada[26]), .CLK(CLK), .L_PRE_100dd675(L_PRE_100dd675[26]), .L_CLR_53bffd8b(L_CLR_53bffd8b[26]),
    .Q(Salida[26]));  // open: L_Q_e415d1a6
  D_FlipFlop_Des_04483694 d_flipflop_des_04483694_7 (
    .D(Entrada[25]), .CLK(CLK), .L_PRE_100dd675(L_PRE_100dd675[25]), .L_CLR_53bffd8b(L_CLR_53bffd8b[25]),
    .Q(Salida[25]));  // open: L_Q_e415d1a6
  D_FlipFlop_Des_04483694 d_flipflop_des_04483694_8 (
    .D(Entrada[24]), .CLK(CLK), .L_PRE_100dd675(L_PRE_100dd675[24]), .L_CLR_53bffd8b(L_CLR_53bffd8b[24]),
    .Q(Salida[24]));  // open: L_Q_e415d1a6
  D_FlipFlop_Des_04483694 d_flipflop_des_04483694_9 (
    .D(Entrada[23]), .CLK(CLK), .L_PRE_100dd675(L_PRE_100dd675[23]), .L_CLR_53bffd8b(L_CLR_53bffd8b[23]),
    .Q(Salida[23]));  // open: L_Q_e415d1a6
  D_FlipFlop_Des_04483694 d_flipflop_des_04483694_10 (
    .D(Entrada[22]), .CLK(CLK), .L_PRE_100dd675(L_PRE_100dd675[22]), .L_CLR_53bffd8b(L_CLR_53bffd8b[22]),
    .Q(Salida[22]));  // open: L_Q_e415d1a6
  D_FlipFlop_Des_04483694 d_flipflop_des_04483694_11 (
    .D(Entrada[21]), .CLK(CLK), .L_PRE_100dd675(L_PRE_100dd675[21]), .L_CLR_53bffd8b(L_CLR_53bffd8b[21]),
    .Q(Salida[21]));  // open: L_Q_e415d1a6
  D_FlipFlop_Des_04483694 d_flipflop_des_04483694_12 (
    .D(Entrada[20]), .CLK(CLK), .L_PRE_100dd675(L_PRE_100dd675[20]), .L_CLR_53bffd8b(L_CLR_53bffd8b[20]),
    .Q(Salida[20]));  // open: L_Q_e415d1a6
  D_FlipFlop_Des_04483694 d_flipflop_des_04483694_13 (
    .D(Entrada[19]), .CLK(CLK), .L_PRE_100dd675(L_PRE_100dd675[19]), .L_CLR_53bffd8b(L_CLR_53bffd8b[19]),
    .Q(Salida[19]));  // open: L_Q_e415d1a6
  D_FlipFlop_Des_04483694 d_flipflop_des_04483694_14 (
    .D(Entrada[18]), .CLK(CLK), .L_PRE_100dd675(L_PRE_100dd675[18]), .L_CLR_53bffd8b(L_CLR_53bffd8b[18]),
    .Q(Salida[18]));  // open: L_Q_e415d1a6
  D_FlipFlop_Des_04483694 d_flipflop_des_04483694_15 (
    .D(Entrada[17]), .CLK(CLK), .L_PRE_100dd675(L_PRE_100dd675[17]), .L_CLR_53bffd8b(L_CLR_53bffd8b[17]),
    .Q(Salida[17]));  // open: L_Q_e415d1a6
  D_FlipFlop_Des_04483694 d_flipflop_des_04483694_16 (
    .D(Entrada[16]), .CLK(CLK), .L_PRE_100dd675(L_PRE_100dd675[16]), .L_CLR_53bffd8b(L_CLR_53bffd8b[16]),
    .Q(Salida[16]));  // open: L_Q_e415d1a6
  D_FlipFlop_Des_04483694 d_flipflop_des_04483694_17 (
    .D(Entrada[15]), .CLK(CLK), .L_PRE_100dd675(L_PRE_100dd675[15]), .L_CLR_53bffd8b(L_CLR_53bffd8b[15]),
    .Q(Salida[15]));  // open: L_Q_e415d1a6
  D_FlipFlop_Des_04483694 d_flipflop_des_04483694_18 (
    .D(Entrada[14]), .CLK(CLK), .L_PRE_100dd675(L_PRE_100dd675[14]), .L_CLR_53bffd8b(L_CLR_53bffd8b[14]),
    .Q(Salida[14]));  // open: L_Q_e415d1a6
  D_FlipFlop_Des_04483694 d_flipflop_des_04483694_19 (
    .D(Entrada[13]), .CLK(CLK), .L_PRE_100dd675(L_PRE_100dd675[13]), .L_CLR_53bffd8b(L_CLR_53bffd8b[13]),
    .Q(Salida[13]));  // open: L_Q_e415d1a6
  D_FlipFlop_Des_04483694 d_flipflop_des_04483694_20 (
    .D(Entrada[12]), .CLK(CLK), .L_PRE_100dd675(L_PRE_100dd675[12]), .L_CLR_53bffd8b(L_CLR_53bffd8b[12]),
    .Q(Salida[12]));  // open: L_Q_e415d1a6
  D_FlipFlop_Des_04483694 d_flipflop_des_04483694_21 (
    .D(Entrada[11]), .CLK(CLK), .L_PRE_100dd675(L_PRE_100dd675[11]), .L_CLR_53bffd8b(L_CLR_53bffd8b[11]),
    .Q(Salida[11]));  // open: L_Q_e415d1a6
  D_FlipFlop_Des_04483694 d_flipflop_des_04483694_22 (
    .D(Entrada[10]), .CLK(CLK), .L_PRE_100dd675(L_PRE_100dd675[10]), .L_CLR_53bffd8b(L_CLR_53bffd8b[10]),
    .Q(Salida[10]));  // open: L_Q_e415d1a6
  D_FlipFlop_Des_04483694 d_flipflop_des_04483694_23 (
    .D(Entrada[9]), .CLK(CLK), .L_PRE_100dd675(L_PRE_100dd675[9]), .L_CLR_53bffd8b(L_CLR_53bffd8b[9]),
    .Q(Salida[9]));  // open: L_Q_e415d1a6
  D_FlipFlop_Des_04483694 d_flipflop_des_04483694_24 (
    .D(Entrada[8]), .CLK(CLK), .L_PRE_100dd675(L_PRE_100dd675[8]), .L_CLR_53bffd8b(L_CLR_53bffd8b[8]),
    .Q(Salida[8]));  // open: L_Q_e415d1a6
  D_FlipFlop_Des_04483694 d_flipflop_des_04483694_25 (
    .D(Entrada[7]), .CLK(CLK), .L_PRE_100dd675(L_PRE_100dd675[7]), .L_CLR_53bffd8b(L_CLR_53bffd8b[7]),
    .Q(Salida[7]));  // open: L_Q_e415d1a6
  D_FlipFlop_Des_04483694 d_flipflop_des_04483694_26 (
    .D(Entrada[6]), .CLK(CLK), .L_PRE_100dd675(L_PRE_100dd675[6]), .L_CLR_53bffd8b(L_CLR_53bffd8b[6]),
    .Q(Salida[6]));  // open: L_Q_e415d1a6
  D_FlipFlop_Des_04483694 d_flipflop_des_04483694_27 (
    .D(Entrada[5]), .CLK(CLK), .L_PRE_100dd675(L_PRE_100dd675[5]), .L_CLR_53bffd8b(L_CLR_53bffd8b[5]),
    .Q(Salida[5]));  // open: L_Q_e415d1a6
  D_FlipFlop_Des_04483694 d_flipflop_des_04483694_28 (
    .D(Entrada[4]), .CLK(CLK), .L_PRE_100dd675(L_PRE_100dd675[4]), .L_CLR_53bffd8b(L_CLR_53bffd8b[4]),
    .Q(Salida[4]));  // open: L_Q_e415d1a6
  D_FlipFlop_Des_04483694 d_flipflop_des_04483694_29 (
    .D(Entrada[3]), .CLK(CLK), .L_PRE_100dd675(L_PRE_100dd675[3]), .L_CLR_53bffd8b(L_CLR_53bffd8b[3]),
    .Q(Salida[3]));  // open: L_Q_e415d1a6
  D_FlipFlop_Des_04483694 d_flipflop_des_04483694_30 (
    .D(Entrada[2]), .CLK(CLK), .L_PRE_100dd675(L_PRE_100dd675[2]), .L_CLR_53bffd8b(L_CLR_53bffd8b[2]),
    .Q(Salida[2]));  // open: L_Q_e415d1a6
  D_FlipFlop_Des_04483694 d_flipflop_des_04483694_31 (
    .D(Entrada[1]), .CLK(CLK), .L_PRE_100dd675(L_PRE_100dd675[1]), .L_CLR_53bffd8b(L_CLR_53bffd8b[1]),
    .Q(Salida[1]));  // open: L_Q_e415d1a6
  D_FlipFlop_Des_04483694 d_flipflop_des_04483694_32 (
    .D(Entrada[0]), .CLK(CLK), .L_PRE_100dd675(L_PRE_100dd675[0]), .L_CLR_53bffd8b(L_CLR_53bffd8b[0]),
    .Q(Salida[0]));  // open: L_Q_e415d1a6
endmodule

module Register_8_bits_Hold_Paralel_Load_15446fa9 (
  input  [7:0] L_PRE_100dd675,
  input  [7:0] Entrada,
  input  LOAD,
  input  CLK,
  input  [7:0] L_CLR_53bffd8b,
  output [7:0] Salida
);

  wire multiplexer_1_out, multiplexer_2_out, multiplexer_3_out, multiplexer_4_out, multiplexer_5_out,
       multiplexer_6_out, multiplexer_7_out, multiplexer_8_out;

  Multiplexer multiplexer_1 (.in0(Salida[7]), .in1(Entrada[7]), .out(multiplexer_1_out), .sel(LOAD));
  D_FlipFlop_Asc_3e1d20b5 d_flipflop_asc_3e1d20b5_1 (
    .D(multiplexer_1_out), .CLK(CLK), .L_CLR_53bffd8b(L_CLR_53bffd8b[7]), .L_PRE_100dd675(L_PRE_100dd675[7]),
    .Q(Salida[7]));  // open: L_Q_e415d1a6
  Multiplexer multiplexer_2 (.in0(Salida[6]), .in1(Entrada[6]), .out(multiplexer_2_out), .sel(LOAD));
  D_FlipFlop_Asc_3e1d20b5 d_flipflop_asc_3e1d20b5_2 (
    .D(multiplexer_2_out), .CLK(CLK), .L_CLR_53bffd8b(L_CLR_53bffd8b[6]), .L_PRE_100dd675(L_PRE_100dd675[6]),
    .Q(Salida[6]));  // open: L_Q_e415d1a6
  Multiplexer multiplexer_3 (.in0(Salida[5]), .in1(Entrada[5]), .out(multiplexer_3_out), .sel(LOAD));
  D_FlipFlop_Asc_3e1d20b5 d_flipflop_asc_3e1d20b5_3 (
    .D(multiplexer_3_out), .CLK(CLK), .L_CLR_53bffd8b(L_CLR_53bffd8b[5]), .L_PRE_100dd675(L_PRE_100dd675[5]),
    .Q(Salida[5]));  // open: L_Q_e415d1a6
  Multiplexer multiplexer_4 (.in0(Salida[4]), .in1(Entrada[4]), .out(multiplexer_4_out), .sel(LOAD));
  D_FlipFlop_Asc_3e1d20b5 d_flipflop_asc_3e1d20b5_4 (
    .D(multiplexer_4_out), .CLK(CLK), .L_CLR_53bffd8b(L_CLR_53bffd8b[4]), .L_PRE_100dd675(L_PRE_100dd675[4]),
    .Q(Salida[4]));  // open: L_Q_e415d1a6
  Multiplexer multiplexer_5 (.in0(Salida[3]), .in1(Entrada[3]), .out(multiplexer_5_out), .sel(LOAD));
  D_FlipFlop_Asc_3e1d20b5 d_flipflop_asc_3e1d20b5_5 (
    .D(multiplexer_5_out), .CLK(CLK), .L_CLR_53bffd8b(L_CLR_53bffd8b[3]), .L_PRE_100dd675(L_PRE_100dd675[3]),
    .Q(Salida[3]));  // open: L_Q_e415d1a6
  Multiplexer multiplexer_6 (.in0(Salida[2]), .in1(Entrada[2]), .out(multiplexer_6_out), .sel(LOAD));
  D_FlipFlop_Asc_3e1d20b5 d_flipflop_asc_3e1d20b5_6 (
    .D(multiplexer_6_out), .CLK(CLK), .L_CLR_53bffd8b(L_CLR_53bffd8b[2]), .L_PRE_100dd675(L_PRE_100dd675[2]),
    .Q(Salida[2]));  // open: L_Q_e415d1a6
  Multiplexer multiplexer_7 (.in0(Salida[1]), .in1(Entrada[1]), .out(multiplexer_7_out), .sel(LOAD));
  D_FlipFlop_Asc_3e1d20b5 d_flipflop_asc_3e1d20b5_7 (
    .D(multiplexer_7_out), .CLK(CLK), .L_CLR_53bffd8b(L_CLR_53bffd8b[1]), .Q(Salida[1]));  // open: L_PRE_100dd675, L_Q_e415d1a6
  Multiplexer multiplexer_8 (.in0(Salida[0]), .in1(Entrada[0]), .out(multiplexer_8_out), .sel(LOAD));
  D_FlipFlop_Asc_3e1d20b5 d_flipflop_asc_3e1d20b5_8 (
    .D(multiplexer_8_out), .CLK(CLK), .L_CLR_53bffd8b(L_CLR_53bffd8b[0]), .Q(Salida[0]));  // open: L_PRE_100dd675, L_Q_e415d1a6

  // Notes on the sheet:
  //   Poner en el informe para que sirve paralel hold y flip flop- descendente o ascendente
endmodule

module Register_4_bits_Des_d9ff5b2d (
  input  [3:0] L_PRE_100dd675,
  input  [3:0] Entrada,
  input  CLK,
  input  [3:0] L_CLR_53bffd8b,
  output [3:0] Salida
);

  D_FlipFlop_Des_04483694 d_flipflop_des_04483694_1 (
    .D(Entrada[3]), .CLK(CLK), .L_PRE_100dd675(L_PRE_100dd675[3]), .L_CLR_53bffd8b(L_CLR_53bffd8b[3]),
    .Q(Salida[3]));  // open: L_Q_e415d1a6
  D_FlipFlop_Des_04483694 d_flipflop_des_04483694_2 (
    .D(Entrada[2]), .CLK(CLK), .L_PRE_100dd675(L_PRE_100dd675[2]), .L_CLR_53bffd8b(L_CLR_53bffd8b[2]),
    .Q(Salida[2]));  // open: L_Q_e415d1a6
  D_FlipFlop_Des_04483694 d_flipflop_des_04483694_3 (
    .D(Entrada[1]), .CLK(CLK), .L_PRE_100dd675(L_PRE_100dd675[1]), .L_CLR_53bffd8b(L_CLR_53bffd8b[1]),
    .Q(Salida[1]));  // open: L_Q_e415d1a6
  D_FlipFlop_Des_04483694 d_flipflop_des_04483694_4 (
    .D(Entrada[0]), .CLK(CLK), .L_PRE_100dd675(L_PRE_100dd675[0]), .L_CLR_53bffd8b(L_CLR_53bffd8b[0]),
    .Q(Salida[0]));  // open: L_Q_e415d1a6
endmodule

module MBR_EN_28495f5d (
  input  [7:0] in_1,
  input  MRB,
  input  MBRU,
  output [31:0] Salida_Signada_7cd268af,
  output [31:0] Salida_No_Signada_cc90b148
);

  assign Salida_Signada_7cd268af = MRB ? {{25{in_1[7]}}, in_1[6:0]} : 32'bz;  // Controlled_Buffer controlled_buffer_1
  assign Salida_No_Signada_cc90b148 = MBRU ? {{24{1'b0}}, in_1} : 32'bz;  // Controlled_Buffer controlled_buffer_2
endmodule

module D_FlipFlop_Des_04483694 (
  input  L_PRE_100dd675,
  input  D,
  input  CLK,
  input  L_CLR_53bffd8b,
  output Q,
  output L_Q_e415d1a6
);

  wire d_latch_70c0f4da_1_q, not_1_out;

  D_Latch_70c0f4da d_latch_70c0f4da_1 (
    .D(D), .EN(CLK), .L_PRE_100dd675(L_PRE_100dd675), .L_CLR_53bffd8b(L_CLR_53bffd8b),
    .Q(d_latch_70c0f4da_1_q));  // open: L_Q_e415d1a6
  not not_1 (not_1_out, CLK);
  D_Latch_70c0f4da d_latch_70c0f4da_2 (
    .D(d_latch_70c0f4da_1_q), .EN(not_1_out), .L_PRE_100dd675(L_PRE_100dd675),
    .L_CLR_53bffd8b(L_CLR_53bffd8b), .Q(Q), .L_Q_e415d1a6(L_Q_e415d1a6));
endmodule

module D_FlipFlop_Asc_3e1d20b5 (
  input  L_PRE_100dd675,
  input  D,
  input  CLK,
  input  L_CLR_53bffd8b,
  output Q,
  output L_Q_e415d1a6
);

  wire nand_1_out, nand_2_out, nand_3_out, nand_4_out, nand_5_out, nand_6_out, not_1_out, not_2_out,
       not_3_out, not_4_out;

  not not_1 (not_1_out, D);
  not not_2 (not_2_out, CLK);
  nand nand_1 (nand_1_out, D, not_2_out);
  nand nand_2 (nand_2_out, not_2_out, not_1_out);
  nand nand_3 (nand_3_out, nand_1_out, L_PRE_100dd675, nand_4_out);
  nand nand_4 (nand_4_out, nand_3_out, L_CLR_53bffd8b, nand_2_out);
  not not_3 (not_3_out, CLK);
  not not_4 (not_4_out, nand_3_out);
  nand nand_5 (nand_5_out, not_3_out, not_4_out);
  nand nand_6 (nand_6_out, nand_3_out, not_3_out);
  nand nand_7 (Q, nand_6_out, L_PRE_100dd675, L_Q_e415d1a6);
  nand nand_8 (L_Q_e415d1a6, Q, L_CLR_53bffd8b, nand_5_out);
endmodule

module D_Latch_70c0f4da (
  input  L_PRE_100dd675,
  input  D,
  input  EN,
  input  L_CLR_53bffd8b,
  output Q,
  output L_Q_e415d1a6
);

  wire and_1_out, and_2_out, not_1_out;

  not not_1 (not_1_out, D);
  and and_1 (and_1_out, D, EN);
  and and_2 (and_2_out, EN, not_1_out);
  and and_3 (Q, and_1_out, L_PRE_100dd675, L_Q_e415d1a6);
  and and_4 (L_Q_e415d1a6, Q, L_CLR_53bffd8b, and_2_out);
endmodule

module ALU_1_bit_fecdfa12 (
  input  Cin,
  input  INVA,
  input  A,
  input  ENA,
  input  B,
  input  ENB,
  input  [1:0] F,
  output Salida,
  output Cout
);

  wire and_1_out, and_2_out, decodificador_1_en1, decodificador_1_en2, decodificador_1_en3,
       decodificador_1_en4, sumador_completo_alu_b48a1a2e_1_s, unidad_logica_alu_2644729c_1_and,
       unidad_logica_alu_2644729c_1_not, unidad_logica_alu_2644729c_1_or, xor_1_out;

  and and_1 (and_1_out, A, ENA);
  and and_2 (and_2_out, B, ENB);
  xor xor_1 (xor_1_out, INVA, and_1_out);
  Decodificador decodificador_1 (
    .F0(F[0]), .F1(F[1]), .EN1(decodificador_1_en1), .EN2(decodificador_1_en2), .EN3(decodificador_1_en3),
    .EN4(decodificador_1_en4));
  Unidad_Logica_ALU_2644729c unidad_logica_alu_2644729c_1 (
    .A(xor_1_out), .B(and_2_out), .EN1(decodificador_1_en1), .EN2(decodificador_1_en2),
    .EN3(decodificador_1_en3), .AND(unidad_logica_alu_2644729c_1_and), .OR(unidad_logica_alu_2644729c_1_or),
    .NOT(unidad_logica_alu_2644729c_1_not));
  Sumador_Completo_ALU_b48a1a2e sumador_completo_alu_b48a1a2e_1 (
    .Cin(Cin), .A(and_2_out), .B(xor_1_out), .EN(decodificador_1_en4), .S(sumador_completo_alu_b48a1a2e_1_s),
    .Cout(Cout));
  or or_1 (Salida, unidad_logica_alu_2644729c_1_and, unidad_logica_alu_2644729c_1_or, unidad_logica_alu_2644729c_1_not, sumador_completo_alu_b48a1a2e_1_s);
endmodule

module Unidad_Logica_ALU_2644729c (
  input  A,
  input  B,
  input  EN1,
  input  EN2,
  input  EN3,
  output AND,
  output OR,
  output NOT
);

  wire and_1_out, not_1_out, or_1_out;

  and and_1 (and_1_out, A, B);
  or or_1 (or_1_out, A, B);
  not not_1 (not_1_out, B);
  and and_2 (AND, and_1_out, EN1);
  and and_3 (OR, or_1_out, EN2);
  and and_4 (NOT, not_1_out, EN3);
endmodule

module Sumador_Completo_ALU_b48a1a2e (
  input  Cin,
  input  A,
  input  B,
  input  EN,
  output S,
  output Cout
);

  wire and_1_out, and_2_out, xor_1_out, xor_2_out;

  and and_1 (and_1_out, EN, B, A);
  xor xor_1 (xor_1_out, A, B);
  or or_1 (Cout, and_1_out, and_2_out);
  and and_2 (and_2_out, EN, xor_1_out, Cin);
  buf xor_2 (xor_2_out, xor_1_out);  // XOR_Gate
  and and_3 (S, xor_2_out, EN);
endmodule

module Desplazador (
  input  [31:0] Entrada,
  input  SRA1,
  input  SLL8,
  output [31:0] Salida
);

  wire [31:0] multiplexer_1_out;

  Multiplexer #(.width(32)) multiplexer_1 (
    .in0(Entrada), .in1({{2{Entrada[31]}}, Entrada[30:1]}), .out(multiplexer_1_out), .sel(SRA1));
  Multiplexer #(.width(32)) multiplexer_2 (
    .in0(multiplexer_1_out), .in1({multiplexer_1_out[23:0], {8{1'b0}}}), .out(Salida), .sel(SLL8));

  // Notes on the sheet:
  //   Nunca sale la combinación 11 
endmodule

module Decodificador (
  input  F0,
  input  F1,
  output EN1,
  output EN2,
  output EN3,
  output EN4
);

  wire not_1_out, not_2_out, not_3_out, not_4_out;

  not not_1 (not_1_out, F0);
  not not_2 (not_2_out, F0);
  not not_3 (not_3_out, F1);
  not not_4 (not_4_out, F1);
  and and_1 (EN1, not_1_out, not_4_out);
  and and_2 (EN2, not_2_out, F1);
  and and_3 (EN3, F0, not_3_out);
  and and_4 (EN4, F0, F1);
endmodule

module ALU_8_bits (
  input  [7:0] B,
  input  [7:0] A,
  input  Cin,
  input  INVA,
  input  ENA,
  input  ENB,
  input  [1:0] F,
  output Cout,
  output [7:0] S
);

  wire alu_1_bit_fecdfa12_1_cout, alu_1_bit_fecdfa12_2_cout, alu_1_bit_fecdfa12_3_cout,
       alu_1_bit_fecdfa12_4_cout, alu_1_bit_fecdfa12_5_cout, alu_1_bit_fecdfa12_6_cout,
       alu_1_bit_fecdfa12_7_cout;
  wire [1:0] undriven, undriven_2;

  ALU_1_bit_fecdfa12 alu_1_bit_fecdfa12_1 (
    .Cin(Cin), .INVA(INVA), .A(A[7]), .ENA(ENA), .B(B[0]), .ENB(ENB), .F(F), .Salida(S[7]),
    .Cout(alu_1_bit_fecdfa12_1_cout));
  ALU_1_bit_fecdfa12 alu_1_bit_fecdfa12_2 (
    .Cin(alu_1_bit_fecdfa12_1_cout), .INVA(INVA), .A(A[6]), .ENA(ENA), .B(B[1]), .ENB(ENB), .F(F),
    .Salida(S[6]), .Cout(alu_1_bit_fecdfa12_2_cout));
  ALU_1_bit_fecdfa12 alu_1_bit_fecdfa12_3 (
    .Cin(alu_1_bit_fecdfa12_2_cout), .INVA(INVA), .A(A[5]), .ENA(ENA), .B(B[2]), .ENB(ENB), .F(F),
    .Salida(S[5]), .Cout(alu_1_bit_fecdfa12_3_cout));
  ALU_1_bit_fecdfa12 alu_1_bit_fecdfa12_4 (
    .Cin(alu_1_bit_fecdfa12_3_cout), .INVA(INVA), .A(A[4]), .ENA(ENA), .B(B[3]), .ENB(ENB), .F(F),
    .Salida(S[4]), .Cout(alu_1_bit_fecdfa12_4_cout));
  ALU_1_bit_fecdfa12 alu_1_bit_fecdfa12_5 (
    .Cin(alu_1_bit_fecdfa12_4_cout), .INVA(INVA), .A(A[3]), .ENA(ENA), .B(B[4]), .ENB(ENB), .F(undriven),
    .Salida(S[3]), .Cout(alu_1_bit_fecdfa12_5_cout));
  ALU_1_bit_fecdfa12 alu_1_bit_fecdfa12_6 (
    .Cin(alu_1_bit_fecdfa12_5_cout), .INVA(INVA), .A(A[2]), .ENA(ENA), .B(B[5]), .ENB(ENB), .F(F),
    .Salida(S[2]), .Cout(alu_1_bit_fecdfa12_6_cout));
  ALU_1_bit_fecdfa12 alu_1_bit_fecdfa12_7 (
    .Cin(alu_1_bit_fecdfa12_6_cout), .INVA(INVA), .A(A[1]), .ENA(ENA), .B(B[6]), .ENB(ENB), .F(undriven_2),
    .Salida(S[1]), .Cout(alu_1_bit_fecdfa12_7_cout));
  ALU_1_bit_fecdfa12 alu_1_bit_fecdfa12_8 (
    .Cin(alu_1_bit_fecdfa12_7_cout), .INVA(INVA), .A(A[0]), .ENA(ENA), .B(B[7]), .ENB(ENB), .F(F),
    .Salida(S[0]), .Cout(Cout));
endmodule

module ALU_32bits (
  input  [31:0] B,
  input  [31:0] A,
  input  Cin,
  input  INVA,
  input  ENA,
  input  ENB,
  input  [1:0] F0_F1_db35ba42,
  output COUT,
  output [31:0] S
);

  wire alu_8_bits_1_cout, alu_8_bits_2_cout, alu_8_bits_3_cout;

  ALU_8_bits alu_8_bits_1 (
    .B(B[7:0]), .A(A[31:24]), .Cin(Cin), .INVA(INVA), .ENA(ENA), .ENB(ENB), .F(F0_F1_db35ba42),
    .Cout(alu_8_bits_1_cout), .S(S[31:24]));
  ALU_8_bits alu_8_bits_2 (
    .B(B[15:8]), .A(A[23:16]), .Cin(alu_8_bits_1_cout), .INVA(INVA), .ENA(ENA), .ENB(ENB),
    .F(F0_F1_db35ba42), .Cout(alu_8_bits_2_cout), .S(S[23:16]));
  ALU_8_bits alu_8_bits_3 (
    .B(B[23:16]), .A(A[15:8]), .Cin(alu_8_bits_2_cout), .INVA(INVA), .ENA(ENA), .ENB(ENB),
    .F(F0_F1_db35ba42), .Cout(alu_8_bits_3_cout), .S(S[15:8]));
  ALU_8_bits alu_8_bits_4 (
    .B(B[31:24]), .A(A[7:0]), .Cin(alu_8_bits_3_cout), .INVA(INVA), .ENA(ENA), .ENB(ENB), .F(F0_F1_db35ba42),
    .Cout(COUT), .S(S[7:0]));
endmodule

module desplazador_MAR (
  input  [31:0] ENTRADA,
  output [31:0] SALIDA
);


  assign SALIDA = {ENTRADA[29:0], 2'b00};
endmodule
