// Logisim project proyecto.circ as structural Verilog: 9 circuits, main circuit main
module main (
);


  // Notes on the sheet:
  //   PAsar todo a MIC-1 con ese MAIN
endmodule

module Registro_32_bits (
  input  [31:0] Entrada_Bus_C,
  input  LOAD,
  input  CLK,
  output [31:0] Salida
);

  wire [31:0] multiplexer_1_out;

  Multiplexer #(.width(32)) multiplexer_1 (.in0(Salida), .in1(Entrada_Bus_C), .out(multiplexer_1_out), .sel(LOAD));
  Register #(.width(32)) register_1 (.D(multiplexer_1_out), .clk(CLK), .Q(Salida));  // open: en, clr

  // Notes on the sheet:
  //   Ver como esta hecho por el profe
endmodule

module Data_Path (
  input  [31:0] Entrada_Bus_C,
  input  Enable_MDR,
  input  Enable_PC,
  input  [7:0] Entrada_MBR,
  input  Enable_MBR_Signo,
  input  Enable_MBRU,
  input  Enable_SP,
  input  Enable_LV,
  input  Enable_CPP,
  input  Enable_TOS,
  input  Enable_OPC,
  input  in_12,
  input  in_13,
  input  in_14,
  input  in_15,
  input  in_16,
  input  in_17,
  output [31:0] Salida_MAR,
  output [31:0] Salida_MDR_Memoria,
  output [31:0] Salida_PC_Memoria,
  output N,
  output Z
);

  wire [31:0] CPP_salida, H_salida, LV_salida, mbr_1_salida_mbr_signo, mbr_1_salida_mbru, MDR_salida,
       OPC_salida, PC_salida, SP_salida, TOS_salida;

  Registro_32_bits MAR (.Entrada_Bus_C(Entrada_Bus_C), .Salida(Salida_MAR));  // open: LOAD, CLK
  Registro_32_bits MDR (.Entrada_Bus_C(Entrada_Bus_C), .Salida(MDR_salida));  // open: LOAD, CLK
  Registro_32_bits PC (.Entrada_Bus_C(Entrada_Bus_C), .Salida(PC_salida));  // open: LOAD, CLK
  MBR mbr_1 (
    .Entrada_Memoria(Entrada_MBR), .Salida_MBR_Signo(mbr_1_salida_mbr_signo), .Salida_MBRU(mbr_1_salida_mbru));  // open: LOAD_MBR, CLK
  Registro_32_bits SP (.Entrada_Bus_C(Entrada_Bus_C), .Salida(SP_salida));  // open: LOAD, CLK
  Registro_32_bits LV (.Entrada_Bus_C(Entrada_Bus_C), .Salida(LV_salida));  // open: LOAD, CLK
  Registro_32_bits CPP (.Entrada_Bus_C(Entrada_Bus_C), .Salida(CPP_salida));  // open: LOAD, CLK
  Registro_32_bits TOS (.Entrada_Bus_C(Entrada_Bus_C), .Salida(TOS_salida));  // open: LOAD, CLK
  Registro_32_bits OPC (.Entrada_Bus_C(Entrada_Bus_C), .Salida(OPC_salida));  // open: LOAD, CLK
  Registro_32_bits H (.Entrada_Bus_C(Entrada_Bus_C), .Salida(H_salida));  // open: LOAD, CLK
  assign Salida_MDR_Memoria = Enable_MDR ? MDR_salida : 32'bz;  // Controlled_Buffer controlled_buffer_1
  assign Salida_MDR_Memoria = Enable_PC ? PC_salida : 32'bz;  // Controlled_Buffer controlled_buffer_2
  assign Salida_MDR_Memoria = Enable_MBR_Signo ? mbr_1_salida_mbr_signo : 32'bz;  // Controlled_Buffer controlled_buffer_3
  assign Salida_MDR_Memoria = Enable_MBRU ? mbr_1_salida_mbru : 32'bz;  // Controlled_Buffer controlled_buffer_4
  assign Salida_MDR_Memoria = Enable_SP ? SP_salida : 32'bz;  // Controlled_Buffer controlled_buffer_5
  assign Salida_MDR_Memoria = Enable_LV ? LV_salida : 32'bz;  // Controlled_Buffer controlled_buffer_6
  assign Salida_MDR_Memoria = Enable_CPP ? CPP_salida : 32'bz;  // Controlled_Buffer controlled_buffer_7
  assign Salida_MDR_Memoria = Enable_TOS ? TOS_salida : 32'bz;  // Controlled_Buffer controlled_buffer_8
  assign Salida_MDR_Memoria = Enable_OPC ? OPC_salida : 32'bz;  // Controlled_Buffer controlled_buffer_9
  ALU_32_bits alu_32_bits_1 (
    .A(H_salida), .ENA(in_12), .INVA(in_13), .B(Salida_MDR_Memoria), .ENB(in_14), .cin(in_15), .F1(in_16),
    .F0(in_17), .count(N));  // open: F_out
  not not_1 (Z, N);

  assign Salida_PC_Memoria = Salida_MDR_Memoria;

  // Notes on the sheet:
  //   Conectar Entrada_Bus_C a la salida del Shifter
  //   Conectar clk
  //   Tiene que estar desplazado 4 bits
  //   Puntos de conexion
  //   Conectar Bus B a la entrada B de la ALU
  //   Conectar Salida_H a la entrada A de la ALU
  //   Salidas MAR/MDR/PC: Conectar a los puertos de la memoria principal.
  //   Conectar y ver shifter
  //   BORRAR TODOS LOS TEXTOS EN NEGRO QUE PUSE CUANDO TERMINEN, LOS PUSE PARA QUE SE GUIEN
endmodule

module Registro_8_bits (
  input  [7:0] Entrada_Bus_C,
  input  LOAD,
  input  CLK,
  output [7:0] Salida
);

  wire [7:0] multiplexer_1_out;

  Multiplexer #(.width(8)) multiplexer_1 (.in0(Salida), .in1(Entrada_Bus_C), .out(multiplexer_1_out), .sel(LOAD));
  Register register_1 (.D(multiplexer_1_out), .clk(CLK), .Q(Salida));  // open: en, clr
endmodule

module MBR (
  input  [7:0] Entrada_Memoria,
  input  LOAD_MBR,
  input  CLK,
  output [31:0] Salida_MBR_Signo,
  output [31:0] Salida_MBRU
);

  Registro_8_bits registro_8_bits_1 (
    .Entrada_Bus_C(Entrada_Memoria), .LOAD(LOAD_MBR), .CLK(CLK), .Salida(Salida_MBRU[7:0]));
  assign Salida_MBR_Signo = {{24{Salida_MBRU[7]}}, Salida_MBRU[7:0]};  // Bit_Extender bit_extender_1

  assign Salida_MBRU[31:8] = {24{1'b0}};
endmodule

module ALU_32_bits (
  input  [31:0] A,
  input  ENA,
  input  INVA,
  input  [31:0] B,
  input  ENB,
  input  cin,
  input  F1,
  input  F0,
  output [31:0] F_out,
  output count
);

  wire [31:0] adder_1_out, and_1_out, and_2_out, and_3_out, bit_extender_1_out, bit_extender_2_out,
       multiplexer_1_out, not_1_out, or_1_out;

  assign bit_extender_1_out = {{31{ENA}}, ENA};  // Bit_Extender bit_extender_1
  assign bit_extender_2_out = {{31{ENB}}, ENB};  // Bit_Extender bit_extender_2
  assign and_1_out = A & bit_extender_1_out;  // AND_Gate and_1, 32 bits wide
  assign and_2_out = A & bit_extender_2_out;  // AND_Gate and_2, 32 bits wide
  assign not_1_out = ~and_1_out;  // NOT_Gate not_1, 32 bits wide
  Multiplexer #(.width(32)) multiplexer_1 (.in0(and_1_out), .in1(not_1_out), .out(multiplexer_1_out), .sel(INVA));
  assign and_3_out = and_1_out & and_2_out;  // AND_Gate and_3, 32 bits wide
  assign or_1_out = multiplexer_1_out | and_2_out;  // OR_Gate or_1, 32 bits wide
  Adder #(.width(32)) adder_1 (.a(multiplexer_1_out), .b(and_2_out), .out(adder_1_out), .cin(cin), .cout(count));
  Multiplexer #(.select(2), .width(32)) multiplexer_2 (
    .in0(and_3_out), .in1(or_1_out), .in2(adder_1_out), .in3({32{1'b0}}), .out(F_out), .sel({F1, F0}));

  assign B = A;

  // Notes on the sheet:
  //   a-hab
  //   b-hab
  //   a-lista
endmodule

module ALU_1_bit (
  input  A,
  input  ENA,
  input  INVA,
  input  B,
  input  ENB,
  input  cin,
  input  F1,
  input  F0,
  output F_out,
  output count
);

  wire adder_1_out, and_1_out, and_2_out, and_3_out, multiplexer_1_out, not_1_out, or_1_out;

  and and_1 (and_1_out, A, ENA);
  and and_2 (and_2_out, A, ENB);
  not not_1 (not_1_out, and_1_out);
  Multiplexer multiplexer_1 (.in0(and_1_out), .in1(not_1_out), .out(multiplexer_1_out), .sel(INVA));
  and and_3 (and_3_out, and_1_out, and_2_out);
  or or_1 (or_1_out, multiplexer_1_out, and_2_out);
  Adder #(.width(1)) adder_1 (.a(multiplexer_1_out), .b(and_2_out), .out(adder_1_out), .cin(cin), .cout(count));
  Multiplexer #(.select(2)) multiplexer_2 (
    .in0(and_3_out), .in1(or_1_out), .in2(adder_1_out), .in3(1'b0), .out(F_out), .sel({F1, F0}));

  assign B = A;

  // Notes on the sheet:
  //   a-hab
  //   b-hab
  //   Falta una negacion
  //   a-lista
endmodule

module Shifter_32_bits (
  input  [31:0] Dato,
  input  [4:0] cant,
  input  Izq_Der,
  output [31:0] ALU_y_Shifter
);

  wire [31:0] shifter_1_out, shifter_2_out;

  Shifter #(.width(32)) shifter_1 (.in(Dato), .\dist (cant), .out(shifter_1_out));
  Shifter #(.shift("lr"), .width(32)) shifter_2 (.in(Dato), .\dist (cant), .out(shifter_2_out));
  Multiplexer #(.width(32)) multiplexer_1 (
    .in0(shifter_1_out), .in1(shifter_2_out), .out(ALU_y_Shifter), .sel(Izq_Der));
endmodule

module ALU_y_Shifter (
  input  [31:0] in_1,
  input  in_2,
  input  in_3,
  input  [31:0] in_4,
  input  in_5,
  input  in_6,
  input  in_7,
  input  in_8,
  input  [31:0] in_9,
  input  [4:0] in_10,
  input  Sel_ALU_Shifter,
  output [31:0] out_12
);

  wire [31:0] alu_32_bits_1_f_out, shifter_32_bits_1_alu_y_shifter;

  ALU_32_bits alu_32_bits_1 (
    .A(in_1), .ENA(in_2), .INVA(in_3), .B(in_4), .ENB(in_5), .cin(in_6), .F1(in_7), .F0(in_8),
    .F_out(alu_32_bits_1_f_out));  // open: count
  Shifter_32_bits shifter_32_bits_1 (
    .Dato(in_9), .cant(in_10), .ALU_y_Shifter(shifter_32_bits_1_alu_y_shifter));  // open: Izq_Der
  Multiplexer #(.width(32)) multiplexer_1 (
    .in0(alu_32_bits_1_f_out), .in1(shifter_32_bits_1_alu_y_shifter), .out(out_12), .sel(Sel_ALU_Shifter));
endmodule
